# Fritzing sketch Omnibot Main Controller (saved by Fritzing 1.0.1rc)
breadboards: 2

parts:
  M1 = DOIT Esp32 DevKit v1 (30 pins long, 11 pins width) [part_number=ESP32S-PIN30]
  L298N1 = L298N DC motor driver
  L298N2 = L298N DC motor driver
  LeftServo = Dagu DGServo 9g header (male) [package=THT]
  RightServo = Dagu DGServo 9g header (male) [package=THT]
  IC1 = MCP23017 I2C I/O Expander
  JACK1 = 2.1mm Barrel Jack with Terminal Block
  M2 = DC Motor [voltage_(max)=6V voltage_(min)=3V]  # not connected
  M3 = DC Motor [voltage_(max)=6V voltage_(min)=3V]  # not connected
  M4 = DC Motor [voltage_(max)=6V voltage_(min)=3V]  # not connected
  M5 = DC Motor [voltage_(max)=6V voltage_(min)=3V]  # not connected

nets:
  GND: M1.GND, L298N1.GND, L298N2.GND, LeftServo.gnd, RightServo.gnd, IC1.VSS, IC1.A1, IC1.A2, JACK1.NEG
  N1: M1.D21, IC1.SDA
  N2: M1.D22, IC1.SCL
  N3: M1.D25, LeftServo.pulse
  N4: M1.D26, RightServo.pulse
  N5: M1.D27, L298N2.ENB
  N6: M1.D14, L298N2.ENA
  N7: M1.D12, L298N1.ENB
  N8: M1.D13, L298N1.ENA
  VIN: M1.VIN, L298N2.5V, IC1.VDD, IC1.A0, IC1.RESET
  12V: L298N1.12V, L298N2.12V, JACK1.POS
  VCC: L298N1.5V, LeftServo.Vcc, RightServo.Vcc
  N9: L298N1.IN1, IC1.GPA7
  N10: L298N1.IN2, IC1.GPA6
  N11: L298N1.IN3, IC1.GPA5
  N12: L298N1.IN4, IC1.GPA4
  N13: L298N2.IN1, IC1.GPA0
  N14: L298N2.IN2, IC1.GPA1
  N15: L298N2.IN3, IC1.GPA2
  N16: L298N2.IN4, IC1.GPA3

notes:
  Left Side Motor Driver
  Right Side Motor Driver
  Left Arm Servo^
  ^Right Arm Servo
  To 9.6V Battery Pack

custom parts:
  DOIT Esp32 DevKit v1 (30 pins long, 11 pins width): The DOIT Esp32 DevKit v1 is one of the development board created by DOIT to evaluate the ESP-WROOM-32 module. It is based on the ESP32 microcontroller that boasts Wifi, Bluetooth, Ethernet and Low Power support all in a single chip. (vanepp) made breadboard work, adjusted pin numbering and labels and reduced size of schematic and cleaned up pcb. This chip is 30pins long (2 x15) and 11 pins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
  L298N DC motor driver: 2x DC motor driver with 78M05 positive voltage regulator (7..35 V) L298N: max 46 V, 2 A Set 5 V Enable jumper to enable 5 V regultor (needed for the L298N) and +5 V output at screw terminal or supply external +5 V at screw terminal Set ENA and/or ENB to +5 V to enable motor permanently or supply ENA and/or ENB with PWM signal IN1 and IN2 set rotation directory for motor A (OUT1/OUT2) IN2 and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
  MCP23017 I2C I/O Expander: The MCP23017 uses two i2c pins (these can be shared with other i2c devices), and in exchange gives you 16 general purpose pins. You can set each of 16 pins to be input, output, input with a pullup or open drain. There's even the ability to get an interrupt via an external pin when any of the inputs change so you don't have to keep polling the chip.
