# Fritzing sketch Omnibot remote 1 (saved by Fritzing 1.0.1rc)
breadboards: 1

parts:
  Part1 = Adafruit HUZZAH32 ESP32 Feather [part_number="Adafruit #3405"]
  Part2 = Thumb Joystick
  Part3 = Thumb Joystick
  R1 = Slide Potentiometer [maximum_resistance=10kΩ knob_status=50% power=0.5W package=THT]
  R2 = Slide Potentiometer [maximum_resistance=10kΩ knob_status=50% power=0.5W package=THT]
  LED1 = smd LED [color="Red (633nm)" package="1206 [SMD]"]
  R3 = Resistor [tolerance=±5% resistance=220 package="0603 [SMD]"]
  JP1 = Header 2 [package=r_sw_th]

nets:
  N1: Part1.A4_IO36, Part2.HORZ
  N2: Part1.A3_I39, Part3.VERT
  N3: Part1.A2_I34, Part3.HORZ
  N4: Part1.A1_DAC1, LED1.anode
  GND: Part1.GND, Part2.GND, Part3.GND, R1.leg2, R2.leg2, R3.Pin_1, JP1.2
  VCC: Part1.3.3V, Part2.VCC, Part3.VCC, R1.leg1, R2.leg1
  N5: Part1.EN, JP1.1
  N6: Part1.IO33_A9, R1.wiper
  N7: Part1.IO14_A6, R2.wiper
  N8: LED1.cathode, R3.Pin_0
